// Logisim project 4-bit adder using basic logic gates.circ as structural Verilog: 1 circuit, main circuit main
module main (
  input  A,
  input  B,
  input  Carry_IN,
  output Sum,
  output Carry_OUT
);

  wire and_1_out, and_2_out, and_3_out, and_4_out, and_5_out, and_6_out, not_1_out, not_2_out, not_3_out,
       not_4_out, or_1_out;

  not not_1 (not_1_out, A);
  not not_2 (not_2_out, B);
  and and_1 (and_1_out, not_1_out, B);
  and and_2 (and_2_out, A, not_2_out);
  or or_1 (or_1_out, and_1_out, and_2_out);
  not not_3 (not_3_out, or_1_out);
  not not_4 (not_4_out, Carry_IN);
  and and_3 (and_3_out, not_3_out, Carry_IN);
  and and_4 (and_4_out, or_1_out, not_4_out);
  and and_5 (and_5_out, or_1_out, Carry_IN);
  and and_6 (and_6_out, A, B);
  or or_2 (Sum, and_3_out, and_4_out);
  or or_3 (Carry_OUT, and_5_out, and_6_out);

  // Notes on the sheet:
  //   Figure E.1.2: 4-bit adder using basic logic gates
endmodule
